# Fritzing sketch LCDGame (saved by Fritzing 0.9.0b)
circuit board: 8.46667cm x 5.64444cm
breadboards: 1

parts:
  Part1 = Arduino Uno (Rev3)
  R1 = Resistor [tolerance=±5% resistance=220 package=THT]
  R2 = Resistor [tolerance=±5% resistance=220 package=THT]
  R3 = Resistor [tolerance=±5% resistance=220 package=THT]
  R4 = Resistor [tolerance=±5% resistance=220 package=THT]
  R5 = Resistor [tolerance=±5% resistance=220 package=THT]
  R6 = Resistor [tolerance=±5% resistance=220 package=THT]
  R7 = Resistor [tolerance=±5% resistance=220 package=THT]
  R8 = Resistor [tolerance=±5% resistance=220 package=THT]
  LED1_1 = LED - 5mm [color="Green (565nm)" package="5 mm [THT]"]
  LED1_2 = LED - 5mm [color="Green (565nm)" package="5 mm [THT]"]
  LED1_3 = LED - 5mm [color="Green (565nm)" package="5 mm [THT]"]
  LED3_1 = LED - 5mm [color="Red (633nm)" package="5 mm [THT]"]
  LED3_2 = LED - 5mm [color="Red (633nm)" package="5 mm [THT]"]
  LED2_3 = LED - 5mm [color="Green (565nm)" package="5 mm [THT]"]
  LED2_2 = LED - 5mm [color="Green (565nm)" package="5 mm [THT]"]
  LED2_1 = LED - 5mm [color="Green (565nm)" package="5 mm [THT]"]
  Pot = POT [package=pot_alpha_rv16af-20]
  Cap = Electrolytic Capacitor [capacitance=100μF package="0807 [SMD, electrolytic]"]

nets (from the pcb view):
  N1: Part1.A0, Pot.S
  N2: Part1.D8, LED2_3.anode
  N3: Part1.D9_PWM, LED2_2.anode
  N4: Part1.D10_PWM/SS, R2.Pin_0, LED2_1.cathode, LED2_1.anode
  N5: Part1.D11_PWM/MOSI, LED1_3.anode
  N6: Part1.D12/MISO, LED1_2.anode
  N7: Part1.D13/SCK, R5.Pin_0, LED1_1.cathode, LED1_1.anode
  N8: Part1.GND, R1.Pin_1, R2.Pin_1, R3.Pin_1, R4.Pin_1, R5.Pin_1, R6.Pin_1, R7.Pin_1, R8.Pin_1
  N9: Part1.D6_PWM, LED3_2.anode
  N10: Part1.D7, LED3_1.anode
  N11: Part1.5V, Pot.E, Cap.+
  N12: R1.Pin_0, LED3_1.cathode
  N13: R3.Pin_0, LED1_3.cathode
  N14: R4.Pin_0, LED1_2.cathode
  N15: R6.Pin_0, LED2_3.cathode
  N16: R7.Pin_0, LED3_2.cathode
  N17: R8.Pin_0, LED2_2.cathode
  N18: Pot.A, Cap.-
